// Logisim project CPU.circ as structural Verilog: 25 circuits, main circuit Processor
module Processor (
);

  wire and_1_out, and_2_out, and_3_out, and_4_out, businterface_1_bm0, businterface_1_bm1,
       businterface_1_bm2, businterface_1_bm3, businterface_1_nrw, businterface_1_strobe, button_1_out,
       button_2_out, button_3_out, button_4_out, button_5_out, CLK, clock_1_out, comparator_1_eq,
       comparator_2_eq, comparator_3_eq, EAL, EPL, EQ, fetchunit_1_ldsx, fetchunit_1_load0,
       fetchunit_1_load1, fetchunit_1_pce, fetchunit_1_store0, fetchunit_1_store1, instructiondecoder_1_hold,
       instructiondecoder_1_ld0, instructiondecoder_1_ld1, instructiondecoder_1_st0,
       instructiondecoder_1_st1, instructiondecoder_1_sx, INT, JMP, LCS, LDR, LNK, LT, LTU, not_1_out,
       not_2_out, OPI, RDY, REL, RST;
  wire [3:0] binarytobcd_1_vout;
  wire [4:0] RD, RS1, RS2, SEL;
  wire [13:0] businterface_1_a_2;
  wire [15:0] businterface_1_a, register_1_q, register_2_q;
  wire [31:0] ALU, binarytobcd_2_vout, binarytobcd_3_vout, binarytobcd_4_vout, binarytobcd_5_vout,
       binarytobcd_6_vout, binarytobcd_7_vout, binarytobcd_8_vout, binarytobcd_9_vout, bit_extender_1_out,
       bit_extender_2_out, CSR, fetchunit_1_addr, fetchunit_1_instr, IMM, MDI, multiplexer_1_out, NPC, PC,
       ram_1_data, register_3_q, RES, rom_1_data, RX, RY, shifter_1_out, shifter_2_out;
  wire [31:4] binarytobcd_1_vout_2;

  _7_Segment_Display u_7_segment_display_1 ();  // open: g, f, a, b, e, d, c, dp
  // BCD_to_7_Segment_decoder bcd_to_7_segment_decoder_1: pin names not known
  not not_1 (not_1_out, not_2_out);
  assign bit_extender_1_out = {{2{businterface_1_a_2[13]}}, {businterface_1_a_2, businterface_1_a}};  // Bit_Extender bit_extender_1
  _7_Segment_Display u_7_segment_display_2 ();  // open: g, f, a, b, e, d, c, dp
  _7_Segment_Display u_7_segment_display_3 ();  // open: g, f, a, b, e, d, c, dp
  // BCD_to_7_Segment_decoder bcd_to_7_segment_decoder_2: pin names not known
  // BCD_to_7_Segment_decoder bcd_to_7_segment_decoder_3: pin names not known
  BinaryToBCD binarytobcd_1 (
    .VOUT({binarytobcd_1_vout_2, binarytobcd_1_vout}), .VIN(binarytobcd_2_vout));  // open: DIGIT
  BinaryToBCD binarytobcd_2 (.VOUT(binarytobcd_2_vout), .VIN(binarytobcd_3_vout));  // open: DIGIT
  Comparator #(.width(14)) comparator_1 (.a(businterface_1_a_2), .b({14{1'b1}}), .eq(comparator_1_eq));  // open: gt, lt
  Comparator #(.width(14)) comparator_2 (.a(businterface_1_a_2), .b({14{1'b0}}), .eq(comparator_2_eq));  // open: gt, lt
  and and_1 (and_1_out, not_1_out, comparator_2_eq);
  and and_2 (and_2_out, comparator_2_eq, not_2_out);
  Shifter #(.width(32)) shifter_1 (.in(bit_extender_1_out), .\dist (5'b00010), .out(shifter_1_out));
  _7_Segment_Display u_7_segment_display_4 ();  // open: g, f, a, b, e, d, c, dp
  // BCD_to_7_Segment_decoder bcd_to_7_segment_decoder_4: pin names not known
  BinaryToBCD binarytobcd_3 (.VOUT(binarytobcd_3_vout), .VIN(binarytobcd_4_vout));  // open: DIGIT
  ROM #(.addrWidth(16), .dataWidth(32)) rom_1 (.addr(register_1_q), .data(rom_1_data));
  Register #(.trigger("high"), .width(16)) register_1 (
    .D(businterface_1_a), .Q(register_1_q), .clk(comparator_1_eq));  // open: en, clr
  RAM #(.addrWidth(16), .asyncread("true"), .byteenables("byteEnables"), .dataWidth(32), .databus("bidir"), .trigger("falling")) ram_1 (
    .addr(register_2_q), .we(and_1_out), .oe(and_2_out), .clk(businterface_1_strobe), .data(ram_1_data),
    .be3(businterface_1_bm3), .be2(businterface_1_bm2), .be1(businterface_1_bm1), .be0(businterface_1_bm0));
  Register #(.trigger("high"), .width(16)) register_2 (
    .D(businterface_1_a), .Q(register_2_q), .clk(comparator_2_eq));  // open: en, clr
  Comparator #(.width(32)) comparator_3 (.a(shifter_1_out), .b(32'hc008000), .eq(comparator_3_eq));  // open: gt, lt
  _7_Segment_Display u_7_segment_display_5 ();  // open: g, f, a, b, e, d, c, dp
  _7_Segment_Display u_7_segment_display_6 ();  // open: g, f, a, b, e, d, c, dp
  // BCD_to_7_Segment_decoder bcd_to_7_segment_decoder_5: pin names not known
  // BCD_to_7_Segment_decoder bcd_to_7_segment_decoder_6: pin names not known
  BinaryToBCD binarytobcd_4 (.VOUT(binarytobcd_4_vout), .VIN(binarytobcd_5_vout));  // open: DIGIT
  BinaryToBCD binarytobcd_5 (.VOUT(binarytobcd_5_vout), .VIN(binarytobcd_6_vout));  // open: DIGIT
  Register #(.width(32)) register_3 (
    .D(ram_1_data), .en(and_3_out), .clk(businterface_1_strobe), .Q(register_3_q));  // open: clr
  and and_3 (and_3_out, ~not_2_out, comparator_3_eq);  // AND_Gate
  _7_Segment_Display u_7_segment_display_7 ();  // open: g, f, a, b, e, d, c, dp
  _7_Segment_Display u_7_segment_display_8 ();  // open: g, f, a, b, e, d, c, dp
  // BCD_to_7_Segment_decoder bcd_to_7_segment_decoder_7: pin names not known
  // BCD_to_7_Segment_decoder bcd_to_7_segment_decoder_8: pin names not known
  BinaryToBCD binarytobcd_6 (.VOUT(binarytobcd_6_vout), .VIN(binarytobcd_7_vout));  // open: DIGIT
  _7_Segment_Display u_7_segment_display_9 ();  // open: g, f, a, b, e, d, c, dp
  // BCD_to_7_Segment_decoder bcd_to_7_segment_decoder_9: pin names not known
  BinaryToBCD binarytobcd_7 (.VOUT(binarytobcd_7_vout), .VIN(binarytobcd_8_vout));  // open: DIGIT
  BinaryToBCD binarytobcd_8 (.VOUT(binarytobcd_8_vout), .VIN(binarytobcd_9_vout));  // open: DIGIT
  assign bit_extender_2_out = {{2{businterface_1_a_2[13]}}, {businterface_1_a_2, businterface_1_a}};  // Bit_Extender bit_extender_2
  _7_Segment_Display u_7_segment_display_10 ();  // open: g, f, a, b, e, d, c, dp
  // BCD_to_7_Segment_decoder bcd_to_7_segment_decoder_10: pin names not known
  BinaryToBCD binarytobcd_9 (.VOUT(binarytobcd_9_vout), .VIN(register_3_q));  // open: DIGIT
  // Probe on shifter_2_out
  Shifter #(.width(32)) shifter_2 (.in(bit_extender_2_out), .\dist (5'b00010), .out(shifter_2_out));
  // Probe on ram_1_data
  assign ram_1_data = and_4_out ? rom_1_data : 32'bz;  // Controlled_Buffer controlled_buffer_1
  and and_4 (and_4_out, comparator_1_eq, not_2_out);
  not not_2 (not_2_out, businterface_1_nrw);
  BusInterface businterface_1 (
    .DIN(MDI), .A({businterface_1_a_2, businterface_1_a}), .STROBE(businterface_1_strobe), .EALIGN(EAL),
    .BM0(businterface_1_bm0), .BM1(businterface_1_bm1), .BM2(businterface_1_bm2), .BM3(businterface_1_bm3),
    .nRW(businterface_1_nrw), .DO(ram_1_data), .DI(ram_1_data), .DOUT(RY), .RST(RST), .CLK(CLK),
    .LDSX(fetchunit_1_ldsx), .LOAD0(fetchunit_1_load0), .LOAD1(fetchunit_1_load1),
    .STORE0(fetchunit_1_store0), .STORE1(fetchunit_1_store1), .ADDR(fetchunit_1_addr));
  RegisterFile registerfile_1 (.Y(RY), .X(RX), .CLK(CLK), .YI(RS2), .WI(RD), .D(RES), .XI(RS1));
  FetchUnit fetchunit_1 (
    .INSTR(fetchunit_1_instr), .ADDR(fetchunit_1_addr), .PC(PC), .PCE(fetchunit_1_pce),
    .LDSX(fetchunit_1_ldsx), .LOAD0(fetchunit_1_load0), .LOAD(LDR), .LOAD1(fetchunit_1_load1),
    .STORE0(fetchunit_1_store0), .STORE1(fetchunit_1_store1), .EMA(ALU), .IPC(NPC), .CLK(CLK), .RST(RST),
    .HOLD(instructiondecoder_1_hold), .SX(instructiondecoder_1_sx), .LD0(instructiondecoder_1_ld0),
    .LD1(instructiondecoder_1_ld1), .ST0(instructiondecoder_1_st0), .ST1(instructiondecoder_1_st1), .DIN(MDI));
  ProgramCounter programcounter_1 (
    .EALIGN(EPL), .PC(NPC), .PCE(fetchunit_1_pce), .CLK(CLK), .JMP(JMP), .ADDR(multiplexer_1_out));
  InstructionDecoder instructiondecoder_1 (
    .RS1(RS1), .LD1(instructiondecoder_1_ld1), .ST0(instructiondecoder_1_st0),
    .ST1(instructiondecoder_1_st1), .ALU_OP(SEL), .PCREL(REL), .OPIMM(OPI), .LINK(LNK),
    .SX(instructiondecoder_1_sx), .LD0(instructiondecoder_1_ld0), .HOLD(instructiondecoder_1_hold),
    .RS2(RS2), .IMM(IMM), .RD(RD), .INSTR(fetchunit_1_instr), .EQ(EQ), .LT(LT), .LTU(LTU), .READY(RDY),
    .CLK(CLK), .RST(RST));  // open: CSR_BIT, CSR_CLR, BRANCH, ILL, CSR_EN, CSRI
  Multiplexer #(.width(32)) multiplexer_1 (.in0(ALU), .in1(32'hfffffff0), .out(multiplexer_1_out), .sel(INT));
  ResultMux resultmux_1 (.RES(RES), .ALU(ALU), .NPC(NPC), .MDI(MDI), .CSR(CSR), .LNK(LNK), .LDR(LDR), .LCS(LCS));
  ArithmeticLogicUnit arithmeticlogicunit_1 (
    .R(ALU), .RDY(RDY), .EQ(EQ), .LT(LT), .LTU(LTU), .SEL(SEL), .A(RX), .PC(PC), .PCREL(REL), .B(RY),
    .IMM(IMM), .OPIMM(OPI), .CLK(CLK));
  Clock clock_1 (.out(clock_1_out));
  Button button_1 (.out(button_1_out));
  T_Flip_Flop t_ff_1 (.T(1'b1), .clk(button_2_out), .Qn(RST));  // open: Q, reset, preset
  Button button_2 (.out(button_2_out));
  T_Flip_Flop t_ff_2 (.T(1'b1), .clk(button_3_out), .Qn(INT));  // open: Q, reset, preset
  Button button_3 (.out(button_3_out));
  or or_1 (CLK, clock_1_out, button_1_out);
  T_Flip_Flop t_ff_3 (.T(1'b1), .clk(button_4_out), .Q(LCS));  // open: Qn, reset, preset
  Button button_4 (.out(button_4_out));
  T_Flip_Flop t_ff_4 (.T(1'b1), .clk(button_5_out), .Qn(JMP));  // open: Q, reset, preset
  Button button_5 (.out(button_5_out));

  // Notes on the sheet:
  //   contents of rom_1 (hex, n*v repeats v):
  //   7ff00793 178793 30479073 340110f3 34006373 3b9ad637 c0085b7 9ff60613 100713 100693 e687b3 f5a023
  //   fef668e3 70693 78713 fedff06f 65516*0 10000113 fffc00b7 8067
endmodule

module RegisterFile (
  input  [31:0] D,
  input  [4:0] WI,
  input  CLK,
  input  [4:0] XI,
  input  [4:0] YI,
  output [31:0] X,
  output [31:0] Y
);

  wire not_1_out, W1, W2, W3, W4, W5, W6, W7, W8, W9, W10, W11, W12, W13, W14, W15, W16, W17, W18, W19, W20,
       W21, W22, W23, W24, W25, W26, W27, W28, W29, W30, W31;
  wire [4:0] bit_extender_1_out, register_1_q, WR;
  wire [31:0] decoder_1_out0, decoder_4_out0, L0_p2, R1, R2, R3, R4, R5, R6, R7, R8, R9, R10, R11, R12, R13,
       R14, R15, R16, R17, R18, R19, R20, R21, R22, R23, R24, R25, R26, R27, R28, R29, R30, R31;

  Decoder #(.enable("false"), .select(5)) decoder_1 (
    .out0(decoder_1_out0[0]), .out1(decoder_1_out0[1]), .out2(decoder_1_out0[2]), .out3(decoder_1_out0[3]),
    .out4(decoder_1_out0[4]), .out5(decoder_1_out0[5]), .out6(decoder_1_out0[6]), .out7(decoder_1_out0[7]),
    .out8(decoder_1_out0[8]), .out9(decoder_1_out0[9]), .out10(decoder_1_out0[10]),
    .out11(decoder_1_out0[11]), .out12(decoder_1_out0[12]), .out13(decoder_1_out0[13]),
    .out14(decoder_1_out0[14]), .out15(decoder_1_out0[15]), .out16(decoder_1_out0[16]),
    .out17(decoder_1_out0[17]), .out18(decoder_1_out0[18]), .out19(decoder_1_out0[19]),
    .out20(decoder_1_out0[20]), .out21(decoder_1_out0[21]), .out22(decoder_1_out0[22]),
    .out23(decoder_1_out0[23]), .out24(decoder_1_out0[24]), .out25(decoder_1_out0[25]),
    .out26(decoder_1_out0[26]), .out27(decoder_1_out0[27]), .out28(decoder_1_out0[28]),
    .out29(decoder_1_out0[29]), .out30(decoder_1_out0[30]), .out31(decoder_1_out0[31]), .sel(XI));
  // RGBLED L31: pin names not known; wires that end beside it: decoder_1_out0[31], L0_p2[31]
  Register #(.trigger("high"), .width(5)) register_1 (.D(WI), .clk(not_1_out), .Q(register_1_q));  // open: en, clr
  not not_1 (not_1_out, CLK);
  assign bit_extender_1_out = {{4{CLK}}, CLK};  // Bit_Extender bit_extender_1
  // RGBLED L30: pin names not known; wires that end beside it: decoder_1_out0[30], L0_p2[30]
  Register #(.trigger("high"), .width(32)) DATA (.D(D), .clk(1'b1));  // open: en, Q, clr
  assign WR = register_1_q & bit_extender_1_out;  // AND_Gate and_1, 5 bits wide
  // RGBLED L29: pin names not known; wires that end beside it: decoder_1_out0[29], L0_p2[29]
  // RGBLED L28: pin names not known; wires that end beside it: decoder_1_out0[28], L0_p2[28]
  Register #(.width(32)) register_2 (.D(D), .clk(W1), .Q(R1));  // open: en, clr
  Register #(.width(32)) register_3 (.D(D), .clk(W2), .Q(R2));  // open: en, clr
  Register #(.width(32)) register_4 (.D(D), .clk(W3), .Q(R3));  // open: en, clr
  // RGBLED L27: pin names not known; wires that end beside it: decoder_1_out0[27], L0_p2[27]
  // RGBLED L26: pin names not known; wires that end beside it: decoder_1_out0[26], L0_p2[26]
  // RGBLED L25: pin names not known; wires that end beside it: decoder_1_out0[25], L0_p2[25]
  Register #(.width(32)) register_5 (.D(D), .clk(W4), .Q(R4));  // open: en, clr
  Register #(.width(32)) register_6 (.D(D), .clk(W5), .Q(R5));  // open: en, clr
  Register #(.width(32)) register_7 (.D(D), .clk(W6), .Q(R6));  // open: en, clr
  Register #(.width(32)) register_8 (.D(D), .clk(W7), .Q(R7));  // open: en, clr
  Decoder #(.enable("false"), .select(5)) decoder_2 (
    .out1(W1), .out2(W2), .out3(W3), .out4(W4), .out5(W5), .out6(W6), .out7(W7), .out8(W8), .out9(W9),
    .out10(W10), .out11(W11), .out12(W12), .out13(W13), .out14(W14), .out15(W15), .out16(W16), .out17(W17),
    .out18(W18), .out19(W19), .out20(W20), .out21(W21), .out22(W22), .out23(W23), .out24(W24), .out25(W25),
    .out26(W26), .out27(W27), .out28(W28), .out29(W29), .out30(W30), .out31(W31), .sel(WR));  // open: out0
  // RGBLED L24: pin names not known; wires that end beside it: decoder_1_out0[24], L0_p2[24]
  // RGBLED L23: pin names not known; wires that end beside it: decoder_1_out0[23], L0_p2[23]
  // RGBLED L22: pin names not known; wires that end beside it: decoder_1_out0[22], L0_p2[22]
  Register #(.width(32)) register_9 (.D(D), .clk(W8), .Q(R8));  // open: en, clr
  Register #(.width(32)) register_10 (.D(D), .clk(W9), .Q(R9));  // open: en, clr
  Register #(.width(32)) register_11 (.D(D), .clk(W10), .Q(R10));  // open: en, clr
  Register #(.width(32)) register_12 (.D(D), .clk(W11), .Q(R11));  // open: en, clr
  // RGBLED L21: pin names not known; wires that end beside it: decoder_1_out0[21], L0_p2[21]
  // RGBLED L20: pin names not known; wires that end beside it: decoder_1_out0[20], L0_p2[20]
  // RGBLED L19: pin names not known; wires that end beside it: decoder_1_out0[19], L0_p2[19]
  // RGBLED L18: pin names not known; wires that end beside it: decoder_1_out0[18], L0_p2[18]
  Register #(.width(32)) register_13 (.D(D), .clk(W12), .Q(R12));  // open: en, clr
  Register #(.width(32)) register_14 (.D(D), .clk(W13), .Q(R13));  // open: en, clr
  Register #(.width(32)) register_15 (.D(D), .clk(W14), .Q(R14));  // open: en, clr
  Register #(.width(32)) register_16 (.D(D), .clk(W15), .Q(R15));  // open: en, clr
  // RGBLED L17: pin names not known; wires that end beside it: decoder_1_out0[17], L0_p2[17]
  Multiplexer #(.select(5), .width(32)) multiplexer_1 (
    .in0({32{1'b0}}), .in1(R1), .in2(R2), .in3(R3), .in4(R4), .in5(R5), .in6(R6), .in7(R7), .in8(R8),
    .in9(R9), .in10(R10), .in11(R11), .in12(R12), .in13(R13), .in14(R14), .in15(R15), .in16(R16), .in17(R17),
    .in18(R18), .in19(R19), .in20(R20), .in21(R21), .in22(R22), .in23(R23), .in24(R24), .in25(R25),
    .in26(R26), .in27(R27), .in28(R28), .in29(R29), .in30(R30), .in31(R31), .out(X), .sel(XI));
  // RGBLED L16: pin names not known; wires that end beside it: decoder_1_out0[16], L0_p2[16]
  // RGBLED L15: pin names not known; wires that end beside it: decoder_1_out0[15], L0_p2[15]
  Register #(.width(32)) register_17 (.D(D), .clk(W16), .Q(R16));  // open: en, clr
  Register #(.width(32)) register_18 (.D(D), .clk(W17), .Q(R17));  // open: en, clr
  Register #(.width(32)) register_19 (.D(D), .clk(W18), .Q(R18));  // open: en, clr
  Register #(.width(32)) register_20 (.D(D), .clk(W19), .Q(R19));  // open: en, clr
  Register #(.trigger("high"), .width(32)) RX (.D(X), .clk(1'b1));  // open: en, Q, clr
  // RGBLED L14: pin names not known; wires that end beside it: decoder_1_out0[14], L0_p2[14]
  // RGBLED L13: pin names not known; wires that end beside it: decoder_1_out0[13], L0_p2[13]
  // RGBLED L12: pin names not known; wires that end beside it: decoder_1_out0[12], L0_p2[12]
  Register #(.width(32)) register_21 (.D(D), .clk(W20), .Q(R20));  // open: en, clr
  Register #(.width(32)) register_22 (.D(D), .clk(W21), .Q(R21));  // open: en, clr
  Register #(.width(32)) register_23 (.D(D), .clk(W22), .Q(R22));  // open: en, clr
  Register #(.width(32)) register_24 (.D(D), .clk(W23), .Q(R23));  // open: en, clr
  // RGBLED L11: pin names not known; wires that end beside it: decoder_1_out0[11], L0_p2[11]
  // RGBLED L10: pin names not known; wires that end beside it: decoder_1_out0[10], L0_p2[10]
  // RGBLED L9: pin names not known; wires that end beside it: decoder_1_out0[9], L0_p2[9]
  Register #(.width(32)) register_25 (.D(D), .clk(W24), .Q(R24));  // open: en, clr
  Register #(.width(32)) register_26 (.D(D), .clk(W25), .Q(R25));  // open: en, clr
  Register #(.width(32)) register_27 (.D(D), .clk(W26), .Q(R26));  // open: en, clr
  Register #(.width(32)) register_28 (.D(D), .clk(W27), .Q(R27));  // open: en, clr
  // RGBLED L8: pin names not known; wires that end beside it: decoder_1_out0[8], L0_p2[8]
  // RGBLED L7: pin names not known; wires that end beside it: decoder_1_out0[7], L0_p2[7]
  // RGBLED L6: pin names not known; wires that end beside it: decoder_1_out0[6], L0_p2[6]
  Register #(.width(32)) register_29 (.D(D), .clk(W28), .Q(R28));  // open: en, clr
  Register #(.width(32)) register_30 (.D(D), .clk(W29), .Q(R29));  // open: en, clr
  Register #(.width(32)) register_31 (.D(D), .clk(W30), .Q(R30));  // open: en, clr
  Register #(.width(32)) register_32 (.D(D), .clk(W31), .Q(R31));  // open: en, clr
  Multiplexer #(.select(5), .width(32)) multiplexer_2 (
    .in0({32{1'b0}}), .in1(R1), .in2(R2), .in3(R3), .in4(R4), .in5(R5), .in6(R6), .in7(R7), .in8(R8),
    .in9(R9), .in10(R10), .in11(R11), .in12(R12), .in13(R13), .in14(R14), .in15(R15), .in16(R16), .in17(R17),
    .in18(R18), .in19(R19), .in20(R20), .in21(R21), .in22(R22), .in23(R23), .in24(R24), .in25(R25),
    .in26(R26), .in27(R27), .in28(R28), .in29(R29), .in30(R30), .in31(R31), .out(Y), .sel(YI));
  // RGBLED L5: pin names not known; wires that end beside it: decoder_1_out0[5], L0_p2[5]
  // RGBLED L4: pin names not known; wires that end beside it: decoder_1_out0[4], L0_p2[4]
  Register #(.trigger("high"), .width(32)) RY (.D(Y), .clk(1'b1));  // open: en, Q, clr
  // RGBLED L3: pin names not known; wires that end beside it: decoder_1_out0[3], L0_p2[3]
  // RGBLED L2: pin names not known; wires that end beside it: decoder_1_out0[2], L0_p2[2]
  // RGBLED L1: pin names not known; wires that end beside it: decoder_1_out0[1], L0_p2[1]
  // RGBLED L0: pin names not known; wires that end beside it: decoder_1_out0[0], L0_p2[0]
  Decoder #(.enable("false"), .select(5)) decoder_3 (
    .out0(L0_p2[0]), .out1(L0_p2[1]), .out2(L0_p2[2]), .out3(L0_p2[3]), .out4(L0_p2[4]), .out5(L0_p2[5]),
    .out6(L0_p2[6]), .out7(L0_p2[7]), .out8(L0_p2[8]), .out9(L0_p2[9]), .out10(L0_p2[10]), .out11(L0_p2[11]),
    .out12(L0_p2[12]), .out13(L0_p2[13]), .out14(L0_p2[14]), .out15(L0_p2[15]), .out16(L0_p2[16]),
    .out17(L0_p2[17]), .out18(L0_p2[18]), .out19(L0_p2[19]), .out20(L0_p2[20]), .out21(L0_p2[21]),
    .out22(L0_p2[22]), .out23(L0_p2[23]), .out24(L0_p2[24]), .out25(L0_p2[25]), .out26(L0_p2[26]),
    .out27(L0_p2[27]), .out28(L0_p2[28]), .out29(L0_p2[29]), .out30(L0_p2[30]), .out31(L0_p2[31]), .sel(YI));
  Decoder #(.enable("false"), .select(5)) decoder_4 (
    .out0(decoder_4_out0[0]), .out1(decoder_4_out0[1]), .out2(decoder_4_out0[2]), .out3(decoder_4_out0[3]),
    .out4(decoder_4_out0[4]), .out5(decoder_4_out0[5]), .out6(decoder_4_out0[6]), .out7(decoder_4_out0[7]),
    .out8(decoder_4_out0[8]), .out9(decoder_4_out0[9]), .out10(decoder_4_out0[10]),
    .out11(decoder_4_out0[11]), .out12(decoder_4_out0[12]), .out13(decoder_4_out0[13]),
    .out14(decoder_4_out0[14]), .out15(decoder_4_out0[15]), .out16(decoder_4_out0[16]),
    .out17(decoder_4_out0[17]), .out18(decoder_4_out0[18]), .out19(decoder_4_out0[19]),
    .out20(decoder_4_out0[20]), .out21(decoder_4_out0[21]), .out22(decoder_4_out0[22]),
    .out23(decoder_4_out0[23]), .out24(decoder_4_out0[24]), .out25(decoder_4_out0[25]),
    .out26(decoder_4_out0[26]), .out27(decoder_4_out0[27]), .out28(decoder_4_out0[28]),
    .out29(decoder_4_out0[29]), .out30(decoder_4_out0[30]), .out31(decoder_4_out0[31]), .sel(WI));

  // Other names for the same wires on the sheet: DI[31:0] = D
endmodule

module ProgramCounter (
  input  PCE,
  input  CLK,
  input  JMP,
  input  [31:0] ADDR,
  output EALIGN,
  output [31:0] PC
);

  wire or_1_out;

  and and_1 (EALIGN, or_1_out, JMP);
  or or_1 (or_1_out, ADDR[0], ADDR[1]);
  Counter #(.max('h3fffffff), .width(30)) counter_1 (
    .load(JMP), .count(PCE), .clk(CLK), .D(ADDR[31:2]), .Q(PC[31:2]));  // open: clr, up, carry
  Register #(.trigger("high"), .width(32)) register_1 (.D({PC[31:2], 2'b00}), .clk(1'b1));  // open: en, Q, clr

  assign PC[1:0] = 2'b00;
endmodule

module ArithmeticLogicUnit (
  input  [31:0] A,
  input  [31:0] PC,
  input  PCREL,
  input  [31:0] B,
  input  [4:0] SEL,
  input  [31:0] IMM,
  input  OPIMM,
  input  CLK,
  output [31:0] R,
  output RDY,
  output EQ,
  output LT,
  output LTU
);

  wire comparator_3_lt, comparator_4_lt, decoder_1_out0, decoder_1_out1, decoder_1_out2, decoder_1_out3,
       decoder_1_out4, decoder_1_out5, decoder_1_out6, decoder_1_out7, decoder_1_out8, decoder_1_out9,
       decoder_1_out10, decoder_1_out11, decoder_1_out12, decoder_1_out13, decoder_1_out14, decoder_1_out15,
       decoder_1_out16, decoder_1_out17, OVF;
  wire [31:0] ANDV, DIFF, multiplier_1_out, ORV, PROD, PRODH, PRODHSU, PRODHU, QUOT, QUOTU, REMS, REMU, SARV,
       shifter_1_out, shifter_2_out, shifter_3_out, SHLV, SHRV, SLTUV, SLTV, SUM, X, XORV, Y;
  wire [32:0] bit_extender_1_out, bit_extender_2_out;
  wire [32:31] multiplier_1_cout;

  assign bit_extender_1_out = {{1{X[31]}}, X};  // Bit_Extender bit_extender_1
  assign bit_extender_2_out = {{1{1'b0}}, Y};  // Bit_Extender bit_extender_2
  Multiplier #(.mode("twosComplement"), .width(33)) multiplier_1 (
    .a(bit_extender_1_out), .b(bit_extender_2_out), .out({PRODHSU[0], multiplier_1_out}),
    .cout({multiplier_1_cout, PRODHSU[31:1]}));  // open: cin
  Adder #(.width(32)) adder_1 (.a(X), .b(Y), .out(SUM));  // open: cin, cout
  Subtractor #(.width(32)) subtractor_1 (.a(X), .b(Y), .out(DIFF));  // open: bin, bout
  Multiplier #(.mode("twosComplement"), .width(32)) multiplier_2 (.a(X), .b(Y), .out(PROD), .cout(PRODH));  // open: cin
  Multiplier #(.width(32)) multiplier_3 (.a(X), .b(Y), .cout(PRODHU));  // open: out, cin
  Divider #(.mode("twosComplement"), .width(32)) divider_1 (.a(X), .b(Y), .out(QUOT), .rem(REMS));  // open: upper
  Divider #(.width(32)) divider_2 (.a(X), .b(Y), .out(QUOTU), .rem(REMU));  // open: upper
  LED F_EQ (.in(EQ));
  Comparator #(.width(32)) comparator_1 (.a(A), .b(B), .eq(EQ), .lt(LT));  // open: gt
  Comparator #(.mode("unsigned"), .width(32)) comparator_2 (.a(A), .b(B), .lt(LTU));  // open: gt, eq
  LED F_LT (.in(LT));
  Register #(.trigger("high"), .width(32)) u_SUM (.D(SUM), .clk(1'b1));  // open: en, Q, clr
  Register #(.trigger("high"), .width(32)) u_DIFF (.D(DIFF), .clk(1'b1));  // open: en, Q, clr
  Register #(.trigger("high"), .width(32)) u_PROD (.D(PROD), .clk(1'b1));  // open: en, Q, clr
  Register #(.trigger("high"), .width(32)) u_PRODH (.D(PRODH), .clk(1'b1));  // open: en, Q, clr
  Register #(.trigger("high"), .width(32)) u_PRODHU (.D(PRODHU), .clk(1'b1));  // open: en, Q, clr
  Register #(.trigger("high"), .width(32)) u_PRODHSU (.D(PRODHSU), .clk(1'b1));  // open: en, Q, clr
  Register #(.trigger("high"), .width(32)) u_QUOT (.D(QUOT), .clk(1'b1));  // open: en, Q, clr
  Register #(.trigger("high"), .width(32)) u_REMS (.D(REMS), .clk(1'b1));  // open: en, Q, clr
  Register #(.trigger("high"), .width(32)) u_QUOTU (.D(QUOTU), .clk(1'b1));  // open: en, Q, clr
  Register #(.trigger("high"), .width(32)) u_REMU (.D(REMU), .clk(1'b1));  // open: en, Q, clr
  LED F_LTU (.in(LTU));
  assign ORV = X | Y;  // OR_Gate or_1, 32 bits wide
  assign ANDV = X & Y;  // AND_Gate and_1, 32 bits wide
  assign XORV = X ^ Y;  // XOR_Gate xor_1, 32 bits wide
  Shifter #(.width(32)) shifter_1 (.in(X), .\dist (Y[4:0]), .out(shifter_1_out));
  Shifter #(.shift("lr"), .width(32)) shifter_2 (.in(X), .\dist (Y[4:0]), .out(shifter_2_out));
  Shifter #(.shift("ar"), .width(32)) shifter_3 (.in(X), .\dist (Y[4:0]), .out(shifter_3_out));
  Comparator #(.width(32)) comparator_3 (.a(X), .b(Y), .lt(comparator_3_lt));  // open: gt, eq
  Comparator #(.mode("unsigned"), .width(32)) comparator_4 (.a(X), .b(Y), .lt(comparator_4_lt));  // open: gt, eq
  Multiplexer #(.width(32)) multiplexer_1 (.in0(shifter_1_out), .in1({32{1'b0}}), .out(SHLV), .sel(OVF));
  Multiplexer #(.width(32)) multiplexer_2 (.in0(shifter_2_out), .in1({32{1'b0}}), .out(SHRV), .sel(OVF));
  Multiplexer #(.width(32)) multiplexer_3 (.in0(shifter_3_out), .in1({32{1'b0}}), .out(SARV), .sel(OVF));
  assign SLTV = {{31{1'b0}}, comparator_3_lt};  // Bit_Extender bit_extender_3
  assign SLTUV = {{31{1'b0}}, comparator_4_lt};  // Bit_Extender bit_extender_4
  Register #(.trigger("high"), .width(32)) u_ORV (.D(ORV), .clk(1'b1));  // open: en, Q, clr
  Register #(.trigger("high"), .width(32)) u_ANDV (.D(ANDV), .clk(1'b1));  // open: en, Q, clr
  Register #(.trigger("high"), .width(32)) u_XORV (.D(XORV), .clk(1'b1));  // open: en, Q, clr
  Register #(.trigger("high"), .width(32)) u_SHLV (.D(SHLV), .clk(1'b1));  // open: en, Q, clr
  Register #(.trigger("high"), .width(32)) u_SHRV (.D(SHRV), .clk(1'b1));  // open: en, Q, clr
  Register #(.trigger("high"), .width(32)) u_SARV (.D(SARV), .clk(1'b1));  // open: en, Q, clr
  Register #(.trigger("high"), .width(32)) u_SLTV (.D(SLTV), .clk(1'b1));  // open: en, Q, clr
  Register #(.trigger("high"), .width(32)) u_SLTUV (.D(SLTUV), .clk(1'b1));  // open: en, Q, clr
  LED F_SUM (.in(decoder_1_out0));
  LED F_DIFF (.in(decoder_1_out1));
  LED F_PROD (.in(decoder_1_out2));
  LED F_PRODH (.in(decoder_1_out3));
  LED F_PRODHU (.in(decoder_1_out4));
  LED F_PRODHSU (.in(decoder_1_out5));
  LED F_QUOT (.in(decoder_1_out6));
  LED F_REMS (.in(decoder_1_out7));
  LED F_QUOTU (.in(decoder_1_out8));
  LED F_REMU (.in(decoder_1_out9));
  LED F_ORV (.in(decoder_1_out10));
  LED F_ANDV (.in(decoder_1_out11));
  LED F_XORV (.in(decoder_1_out12));
  LED F_SHLV (.in(decoder_1_out13));
  LED F_SHRV (.in(decoder_1_out14));
  LED F_SARV (.in(decoder_1_out15));
  LED F_SLTV (.in(decoder_1_out16));
  LED F_SLTUV (.in(decoder_1_out17));
  Multiplexer #(.select(5), .width(32)) multiplexer_4 (
    .in0(SUM), .in1(DIFF), .in2(PROD), .in3(PRODH), .in4(PRODHU), .in5(PRODHSU), .in6(QUOT), .in7(REMS),
    .in8(QUOTU), .in9(REMU), .in10(ORV), .in11(ANDV), .in12(XORV), .in13(SHLV), .in14(SHRV), .in15(SARV),
    .in16(SLTV), .in17(SLTUV), .in18({32{1'b0}}), .in19({32{1'b0}}), .in20({32{1'b0}}), .in21({32{1'b0}}),
    .in22({32{1'b0}}), .in23({32{1'b0}}), .in24({32{1'b0}}), .in25({32{1'b0}}), .in26({32{1'b0}}),
    .in27({32{1'b0}}), .in28({32{1'b0}}), .in29({32{1'b0}}), .in30({32{1'b0}}), .in31({32{1'b0}}), .out(R),
    .sel(SEL));
  Decoder #(.enable("false"), .select(5)) decoder_1 (
    .out0(decoder_1_out0), .out1(decoder_1_out1), .out2(decoder_1_out2), .out3(decoder_1_out3),
    .out4(decoder_1_out4), .out5(decoder_1_out5), .out6(decoder_1_out6), .out7(decoder_1_out7),
    .out8(decoder_1_out8), .out9(decoder_1_out9), .out10(decoder_1_out10), .out11(decoder_1_out11),
    .out12(decoder_1_out12), .out13(decoder_1_out13), .out14(decoder_1_out14), .out15(decoder_1_out15),
    .out16(decoder_1_out16), .out17(decoder_1_out17), .sel(SEL));  // open: out18, out19, out20, out21, out22, out23, out24, out25, out26, out27, out28, out29, out30, out31
  Register #(.trigger("high"), .width(32)) VR (.D(R), .clk(1'b1));  // open: en, Q, clr
  or or_2 (OVF, Y[5], Y[6], Y[7], Y[8], Y[9], Y[10], Y[11], Y[12], Y[13], Y[14], Y[15], Y[16], Y[17], Y[18], Y[19], Y[20], Y[21], Y[22], Y[23], Y[24], Y[25], Y[26], Y[27], Y[28], Y[29], Y[30], Y[31]);
  Register #(.trigger("high"), .width(32)) VX (.D(X), .clk(1'b1));  // open: en, Q, clr
  Multiplexer #(.width(32)) multiplexer_5 (.in0(A), .in1(PC), .out(X), .sel(PCREL));
  LED #(.active("false")) X_A (.in(PCREL));
  LED X_PC (.in(PCREL));
  Register #(.trigger("high"), .width(32)) VY (.D(Y), .clk(1'b1));  // open: en, Q, clr
  Multiplexer #(.width(32)) multiplexer_6 (.in0(B), .in1(IMM), .out(Y), .sel(OPIMM));
  LED #(.active("false")) Y_B (.in(OPIMM));
  LED Y_IMM (.in(OPIMM));
  LED F_READY (.in(1'b1));

  assign RDY = 1'b1;

  // Other names for the same wires on the sheet: VX[31:0] = A; VY[31:0] = B; Y4_0[4:0] = Y[4:0]
endmodule

module MaskingUnit (
  input  M0,
  input  M1,
  input  M2,
  input  [31:0] DI,
  input  M3,
  output [31:0] DO
);

  wire [7:0] bit_extender_1_out, bit_extender_2_out, bit_extender_3_out, bit_extender_4_out;

  assign DO[7:0] = DI[7:0] & bit_extender_1_out;  // AND_Gate and_1, 8 bits wide
  assign bit_extender_1_out = {{7{M0}}, M0};  // Bit_Extender bit_extender_1
  assign DO[15:8] = DI[15:8] & bit_extender_2_out;  // AND_Gate and_2, 8 bits wide
  assign bit_extender_2_out = {{7{M1}}, M1};  // Bit_Extender bit_extender_2
  assign DO[23:16] = DI[23:16] & bit_extender_3_out;  // AND_Gate and_3, 8 bits wide
  assign bit_extender_3_out = {{7{M2}}, M2};  // Bit_Extender bit_extender_3
  assign DO[31:24] = DI[31:24] & bit_extender_4_out;  // AND_Gate and_4, 8 bits wide
  assign bit_extender_4_out = {{7{M3}}, M3};  // Bit_Extender bit_extender_4
endmodule

module LeftShifter (
  input  A0,
  input  A1,
  input  [31:0] DI,
  output [31:0] DO
);

  wire [31:0] multiplexer_1_out, shifter_1_out, shifter_2_out;

  Shifter #(.width(32)) shifter_1 (.in(DI), .\dist (5'b01000), .out(shifter_1_out));
  Multiplexer #(.width(32)) multiplexer_1 (.in0(DI), .in1(shifter_1_out), .out(multiplexer_1_out), .sel(A0));
  Multiplexer #(.width(32)) multiplexer_2 (.in0(multiplexer_1_out), .in1(shifter_2_out), .out(DO), .sel(A1));
  Shifter #(.width(32)) shifter_2 (.in(multiplexer_1_out), .\dist (5'b10000), .out(shifter_2_out));
endmodule

module RightShifter (
  input  A0,
  input  A1,
  input  [31:0] DI,
  output [31:0] DO
);

  wire [31:0] multiplexer_1_out, shifter_1_out, shifter_2_out;

  Shifter #(.shift("ar"), .width(32)) shifter_1 (.in(DI), .\dist (5'b01000), .out(shifter_1_out));
  Multiplexer #(.width(32)) multiplexer_1 (.in0(DI), .in1(shifter_1_out), .out(multiplexer_1_out), .sel(A0));
  Multiplexer #(.width(32)) multiplexer_2 (.in0(multiplexer_1_out), .in1(shifter_2_out), .out(DO), .sel(A1));
  Shifter #(.shift("lr"), .width(32)) shifter_2 (.in(multiplexer_1_out), .\dist (5'b10000), .out(shifter_2_out));
endmodule

module SignExtender (
  input  [31:0] DI,
  input  LB,
  input  LDSX,
  output [31:0] DO
);

  wire and_1_out;
  wire [6:0] bit_extender_1_out;
  wire [15:0] bit_extender_2_out;

  and and_1 (and_1_out, LB, LDSX);
  Multiplexer multiplexer_1 (.in0(DI[15]), .in1(DI[7]), .out(DO[15]), .sel(and_1_out));
  Multiplexer #(.width(7)) multiplexer_2 (.in0(DI[14:8]), .in1(bit_extender_1_out), .out(DO[14:8]), .sel(and_1_out));
  assign bit_extender_1_out = {{6{DI[7]}}, DI[7]};  // Bit_Extender bit_extender_1
  Multiplexer #(.width(16)) multiplexer_3 (.in0(DI[31:16]), .in1(bit_extender_2_out), .out(DO[31:16]), .sel(LDSX));
  assign bit_extender_2_out = {{15{DO[15]}}, DO[15]};  // Bit_Extender bit_extender_2

  assign DO[7:0] = DI[7:0];
endmodule

module BusInterface (
  input  [31:0] DI,
  input  [31:0] DOUT,
  input  RST,
  input  CLK,
  input  LDSX,
  input  LOAD0,
  input  LOAD1,
  input  STORE0,
  input  STORE1,
  input  [31:0] ADDR,
  output [31:0] DIN,
  output [31:0] DO,
  output STROBE,
  output EALIGN,
  output BM0,
  output BM1,
  output BM2,
  output BM3,
  output nRW,
  output [29:0] A
);

  wire LB, LD, not_1_out;
  wire [31:0] bit_extender_1_out, leftshifter_1_do, maskingunit_1_do, maskingunit_2_do, rightshifter_1_do,
       signextender_1_do;

  MaskingUnit maskingunit_1 (.DO(maskingunit_1_do), .DI(DI), .M0(BM0), .M1(BM1), .M2(BM2), .M3(BM3));
  LeftShifter leftshifter_1 (.DO(leftshifter_1_do), .DI(DOUT), .A0(ADDR[0]), .A1(ADDR[1]));
  MaskingUnit maskingunit_2 (.DO(maskingunit_2_do), .DI(leftshifter_1_do), .M0(BM0), .M1(BM1), .M2(BM2), .M3(BM3));
  not not_1 (not_1_out, CLK);
  // PlaRom #(.Contents("0*4 1 2 0*5 2 0*4 2 0*4 2 0*4 2 0*3 1 1 0 0 2 2 1 1 2 0 0 2 1 1 0 2 2 0 1 1 2 2 0 0 2 2 1 0 1 2*3 1 2 1 0 2 1 0 1 2 1 2 1 2 1 0 1 2 1 1 0 1 2 2 1 1 2 1 0 1 1 0 0 2 0 1 1 2 0*3 1 2 1 0 1 2 1 2 1 2 1 0 1 1 0*3 2 1 1 0 2 0*3 2 0 0 2 0 0 2 2 0*3 2 0*3 2*3 0 2 0 0 2 2 0 0 2 2 0 2 0 2 2 0 0 1 0*8 1 0*7 1 0*8 1 0*7 1 0*8 1 1 0*6 1 1 0*6 1 1 0*6 1 1 0*6 1 0*7 1 0*7 1 1 0*6 1 1 0*7 1 0*7 1 0*8 1 1 0*6 1 1 0*6 1 0*7 1 0*8 1 0*7 1 0*8 1 0*7 1 0*7 1 0*7 1 0*7 1 0*7 1"), .\and (27), .outputs(8)) MaskGen: pin names not known; wires that end beside it: {ADDR[1:0], STORE1, STORE0, LOAD1, LOAD0}, {LB, LD, nRW, BM3, BM2, BM1, BM0, EALIGN}
  Register #(.trigger("high"), .width(32)) MAR (.D(ADDR), .clk(1'b1));  // open: en, Q, clr
  RightShifter rightshifter_1 (.DO(rightshifter_1_do), .DI(maskingunit_1_do), .A0(ADDR[0]), .A1(ADDR[1]));
  nor nor_1 (STROBE, RST, not_1_out);
  SignExtender signextender_1 (.DO(signextender_1_do), .DI(rightshifter_1_do), .LB(LB), .LDSX(LDSX));
  Register #(.trigger("high"), .width(32)) MDO (.D(maskingunit_2_do), .clk(nRW));  // open: en, Q, clr
  assign DO = nRW ? maskingunit_2_do : 32'bz;  // Controlled_Buffer controlled_buffer_1
  assign bit_extender_1_out = {{31{LD}}, LD};  // Bit_Extender bit_extender_1
  assign DIN = bit_extender_1_out & signextender_1_do;  // AND_Gate and_1, 32 bits wide
  Register #(.trigger("high"), .width(32)) MDI (.D(DIN), .clk(1'b1));  // open: en, Q, clr

  assign A = ADDR[31:2];

  // Other names for the same wires on the sheet: A0 = ADDR[0]; A1 = ADDR[1]; M0 = BM0; M1 = BM1; M2 = BM2; M3 = BM3;
  //   ST = nRW; SX = LDSX

  // Notes on the sheet:
  //   RST: pull=up
endmodule

module FetchUnit (
  input  RST,
  input  HOLD,
  input  [31:0] DIN,
  input  SX,
  input  [31:0] EMA,
  input  LD0,
  input  [31:0] IPC,
  input  LD1,
  input  ST0,
  input  ST1,
  input  CLK,
  output [31:0] INSTR,
  output PCE,
  output LDSX,
  output LOAD0,
  output [31:0] ADDR,
  output LOAD,
  output LOAD1,
  output [31:0] PC,
  output STORE0,
  output STORE1
);

  wire ISE, not_1_out, or_1_out, PCM;
  wire [31:0] multiplexer_3_out;

  or or_1 (or_1_out, ST1, ST0);
  or or_2 (PCM, or_1_out, LOAD);
  or or_3 (LOAD, LD1, LD0);
  nor nor_1 (PCE, PCM, HOLD, RST);
  or or_4 (ISE, RST, PCE);
  and and_1 (LDSX, LOAD, SX);
  Multiplexer multiplexer_1 (.in0(PCE), .in1(LD0), .out(LOAD0), .sel(LOAD));
  Multiplexer multiplexer_2 (.in0(PCE), .in1(LD1), .out(LOAD1), .sel(LOAD));
  LED FETCHING (.in(PCE));
  Register #(.width(32)) INS (.D(multiplexer_3_out), .en(ISE), .clk(CLK), .Q(INSTR));  // open: clr
  Multiplexer #(.width(32)) multiplexer_3 (.in0(DIN), .in1(32'h13), .out(multiplexer_3_out), .sel(RST));
  Register #(.width(32)) PCR (.D(IPC), .en(PCE), .clk(CLK), .Q(PC));  // open: clr
  not not_1 (not_1_out, PCM);
  Multiplexer #(.width(32)) multiplexer_4 (.in0(EMA), .in1(IPC), .out(ADDR), .sel(not_1_out));

  assign STORE0 = ST0;
  assign STORE1 = ST1;
endmodule

module RegisterDecoder (
  input  [31:0] INSTR,
  output [4:0] RD,
  output IO,
  output [4:0] RS1,
  output [4:0] RS2
);

  wire DE, S1E, S2E;

  // PlaRom #(.Contents("0*3 1 0 0 1 1 0*3 2 2 1 1 0 1 0*3 2 0 1 1 0*3 1*3 2 2 0 1 1 0 2 0 1 1 0*4 2 1*3 0*3 1 2 0 1 1 0*3 1 0 2 1 0*4 2 2 1 0 2 0*4 2 2 1 1 0*3 1 1 0 1 1 0*3 1 0 1*3 1 0*3 1 0*3 1 0*3 1 0 1 0 1 0*4 1 0*3 1 0*4 1 0*3 1 0*3 1 0*3 1 0*4 1"), .\and (12)) RegMask: pin names not known; wires that end beside it: {INSTR[14:12], INSTR[6:2]}, {S1E, S2E, DE, IO}
  assign RD = {5{DE}} & INSTR[11:7];  // AND_Gate and_1, 5 bits wide
  assign RS1 = {5{S1E}} & INSTR[19:15];  // AND_Gate and_2, 5 bits wide
  assign RS2 = {5{S2E}} & INSTR[24:20];  // AND_Gate and_3, 5 bits wide
  Register #(.trigger("high"), .width(5)) V_RD (.D(RD), .clk(1'b1));  // open: en, Q, clr
  Register #(.trigger("high"), .width(5)) V_RS1 (.D(RS1), .clk(1'b1));  // open: en, Q, clr
  Register #(.trigger("high"), .width(5)) V_RS2 (.D(RS2), .clk(1'b1));  // open: en, Q, clr

  // Other names for the same wires on the sheet: P11_7[4:0] = INSTR[11:7]; P19_15[4:0] = INSTR[19:15];
  //   P24_20[4:0] = INSTR[24:20]

  // Notes on the sheet:
  //   OP [6:2]
  //   rd/imm [11:7]
  //   funct3/imm [14:12]
  //   rs1/imm [19:15]
  //   rs2/imm [24:20]
endmodule

module InstructionArbiter (
  input  [31:0] INSTR,
  input  CLK,
  input  HOLD_IN,
  output HOLD
);

  wire and_1_out, comparator_1_eq, comparator_2_eq, d_ff_1_q, IO, or_1_out, or_2_out;
  wire [4:0] R1, R2, RD, register_1_q;

  RegisterDecoder registerdecoder_1 (.RD(RD), .RS1(R1), .RS2(R2), .IO(IO), .INSTR(INSTR));
  Register #(.width(5)) register_1 (.D(RD), .clk(CLK), .Q(register_1_q));  // open: en, clr
  D_Flip_Flop d_ff_1 (.D(IO), .clk(CLK), .Q(d_ff_1_q));  // open: Qn, preset, reset
  Comparator #(.mode("unsigned"), .width(5)) comparator_1 (
    .a(R1), .b(register_1_q), .eq(comparator_1_eq));  // open: gt, lt
  or or_1 (or_1_out, comparator_1_eq, comparator_2_eq);
  Comparator #(.mode("unsigned"), .width(5)) comparator_2 (
    .a(register_1_q), .b(R2), .eq(comparator_2_eq));  // open: gt, lt
  or or_2 (or_2_out, register_1_q[0], register_1_q[1], register_1_q[2], register_1_q[3], register_1_q[4]);
  LED F_HOLD (.in(and_1_out));
  and and_1 (and_1_out, d_ff_1_q, or_1_out, or_2_out);
  or or_3 (HOLD, and_1_out, HOLD_IN);
endmodule

module InstructionValidator (
  input  [31:0] INSTR,
  output ILL
);

  wire and_1_out, and_2_out, FUNCT, nand_1_out, or_1_out, or_2_out, SYS;
  wire [0:0] CHK_p3;
  wire [6:0] CLF_p3;

  nand nand_1 (nand_1_out, INSTR[0], INSTR[1]);
  // PlaRom #(.Contents("1 2 2 1 1 2 2 1 1 2*4 1*4 0 1*5 2 2 1 2 1*3 2 2 1*4 0 2 1 2*3 1 2 2 0 0 2 2 0*4 2 1 2 1 0*3 2 0 2 0 2 1 2 1 0 2 1 0 1 1 2 1 0*7 1 0*6 1 0*6 1 0*6 1 0*7 1 0*7 1 0*7 1 0*7 1 0*7 1 0*6 1 0*6 1 0*6 1 0*6 1 0*6 1"), .\and (15), .outputs(7)) CLF: pin names not known; wires that end beside it: INSTR[6:2], 1'b0, CLF_p3
  // PlaRom #(.Contents("1 0*4 1 2 2 1 1 0 1 2 1 2 1 0 2 1 1 0 0 1*3 2*3 1*4 0 1 2 1 0 2 1 1 0 1*4 0 2 2 1 1 0*7 2 2 0*9 2 1 0*5 2 1 0*8 2 0 2 0 2 0*3 2 0 0 1 0 2 0*3 2 0*3 1 0 2 0*4 2 2 1 0 1 0*6 2 0 0 1 1 2 0 0 2 2 0 0 1 1 0*4 2 0*4 1 1 2 0 0 2 0 0 1 2 1 0*7 1 2 1 0 2 0*5 1 0 1 1 2 0 0 2 1 1 2 0 2 0*4 1 2 0 2 0 1 1 0 2 0 0 2 0 1 2 2 0 1 2 2 0*3 1 2 2 0 1 0 2 0 1 2 0 1 2 0 1 2 0 2 0 1 1 2 0 0 1 2 0 1 1 2 1 0 2 0 1 1 0 0 1 0 0 1 1 0 1 0 0 1 0*4 1 0 0 1 0 0 1 0 0 1 0 0 1 0 0 1 0 0 1 0 0 1 0 0 1 0 0 1 0 0 1 0 0 1 0 0 1 0 0 1 0 0 1 0 0 1 0 0 1 0 0 1 0 0 1 0 0 1"), .\and (25), .outputs(3)) CHK: pin names not known; wires that end beside it: {INSTR[30], INSTR[25], INSTR[14:12], INSTR[6:2]}, 1'b0, {FUNCT, SYS, CHK_p3[0]}
  LED R (.in(CLF_p3[6]));
  or or_1 (or_1_out, INSTR[7], INSTR[8], INSTR[9], INSTR[10], INSTR[11], INSTR[15], INSTR[16], INSTR[17], INSTR[18], INSTR[19]);
  or or_2 (or_2_out, INSTR[31], INSTR[26], INSTR[27], INSTR[28], INSTR[29]);
  LED I (.in(CLF_p3[5]));
  LED S (.in(CLF_p3[4]));
  LED B (.in(CLF_p3[3]));
  LED U (.in(CLF_p3[2]));
  and and_1 (and_1_out, SYS, or_1_out);
  and and_2 (and_2_out, FUNCT, or_2_out);
  LED J (.in(CLF_p3[1]));
  or or_3 (ILL, and_1_out, and_2_out, nand_1_out, CLF_p3[0], CHK_p3[0]);

  // Other names for the same wires on the sheet: P11_7[4:0] = INSTR[11:7]; P19_15[4:0] = INSTR[19:15];
  //   P29_26[3:0] = INSTR[29:26]; P31 = INSTR[31]

  // Notes on the sheet:
  //   1'b1
  //   1'b1
  //   OP [6:2]
  //   rd/imm [11:7]
  //   funct3/imm [14:12]
  //   rs1/imm [19:15]
  //   funct7/imm [25]
  //   funct7/imm [29:26]
  //   funct7/imm [30]
  //   funct7/imm [31]
endmodule

module InstructionDecoder (
  input  READY,
  input  [31:0] INSTR,
  input  CLK,
  input  RST,
  input  EQ,
  input  LT,
  input  LTU,
  output [4:0] RD,
  output [4:0] RS1,
  output [4:0] RS2,
  output [11:0] CSRI,
  output [4:0] ALU_OP,
  output PCREL,
  output OPIMM,
  output BRANCH,
  output LINK,
  output SX,
  output LD0,
  output LD1,
  output ST0,
  output ST1,
  output CSR_EN,
  output CSR_BIT,
  output [31:0] IMM,
  output CSR_CLR,
  output HOLD,
  output ILL
);

  wire and_3_out, and_4_out, BR, COND, CSRI_t, CTR, d_ff_1_qn, DE, ILL_I, multiplexer_1_out,
       multiplexer_2_out, nand_2_out, not_1_out, nSHIFT, REG_WE, S1E, S2E, S4_1_0, S4_1_1, S10_5, S19_12,
       S30_20, X0, X11, X31, xor_1_out;
  wire [3:0] and_9_out, and_10_out, or_2_out;
  wire [4:4] and_1_out;
  wire [5:0] and_11_out, CLF_p2;
  wire [5:5] and_7_out;
  wire [7:0] multiplexer_4_out;
  wire [10:0] multiplexer_5_out;
  wire [11:0] bit_extender_1_out;
  wire [18:0] bit_extender_2_out;
  wire [21:21] rom_1_data;
  wire [31:0] bit_extender_3_out;

  Register #(.trigger("high"), .width(32)) V_INS (.D(INSTR), .clk(1'b1));  // open: en, Q, clr
  and and_1 (and_1_out[4], DE, REG_WE);
  nand nand_1 (ILL_I, INSTR[0], INSTR[1]);
  assign RD = {5{and_1_out[4]}} & INSTR[11:7];  // AND_Gate and_2, 5 bits wide
  Register #(.trigger("high"), .width(5)) V_RD (.D(RD), .clk(1'b1));  // open: en, Q, clr
  // PlaRom #(.Contents("1 2 2 1 1 2 2 1 1 2*4 1*4 0 1*5 2 2 1 2 1*3 2 2 1*4 0 2 1 2*3 1 2 2 1 0*6 1 0*5 1 0*5 1 0*5 1 0*6 1 0*6 1 0*6 1 0*6 1"), .\and (9), .outputs(6)) CLF: pin names not known; wires that end beside it: INSTR[6:2], {CLF_p2[5:3], BR, CLF_p2[1:0]}
  Multiplexer multiplexer_1 (.in0(LT), .in1(LTU), .out(multiplexer_1_out), .sel(INSTR[13]));
  ROM #(.addrWidth(11), .dataWidth(22)) rom_1 (
    .addr({CTR, COND, INSTR[25], INSTR[14:12], INSTR[6:2]}),
    .data({rom_1_data[21], HOLD, CSR_CLR, CSR_BIT, CSRI_t, CSR_EN, ST1, ST0, LD1, LD0, SX, LINK, BRANCH, OPIMM, PCREL, REG_WE, nSHIFT, ALU_OP}));
  LED R (.in(CLF_p2[5]));
  LED I (.in(CLF_p2[4]));
  LED S (.in(CLF_p2[3]));
  nand nand_2 (nand_2_out, READY, CTR);
  D_Flip_Flop d_ff_1 (.D(and_3_out), .clk(CLK), .Q(CTR), .Qn(d_ff_1_qn), .reset(RST));  // open: preset
  and and_3 (and_3_out, nand_2_out, HOLD);
  Multiplexer multiplexer_2 (.in0(EQ), .in1(multiplexer_1_out), .out(multiplexer_2_out), .sel(INSTR[14]));
  and and_4 (and_4_out, xor_1_out, BR);
  LED u_COND (.in(and_4_out));
  assign RS1 = {5{S1E}} & INSTR[19:15];  // AND_Gate and_5, 5 bits wide
  // PlaRom #(.Contents("0*3 1 0 0 1 1 0*3 2 2 1 1 0 1 0*3 2 0 1 1 0*3 1*3 2 2 0 1 1 0 2 0 1 1 0*4 2 1*3 0*3 1 2 0 1 1 0*3 1 0 2 1 0*4 2 2 1 0 2 0*4 2 2 1 1 0*3 1 1 0 1 1 1 0 0 1 0 0 1 0 0 1 0 1 1 0*3 1 0 0 1 0*3 1 0 0 1 0 0 1 0 0 1"), .\and (11), .outputs(3)) RMASK: pin names not known; wires that end beside it: {INSTR[14:12], INSTR[6:2]}, {S1E, S2E, DE}
  // PlaRom #(.Contents("0 0 2 1 2 1*3 0 2 0 2*3 1 1 0 2 0 2 2 1 1 2 0 2 0 1*3 2 2 0 2 0 1 1 0 1 1 0*3 2*3 1 1 0*3 2 2 1 0 2 0*3 1*3 2 2 0*3 1 1 0 1 1 0*4 2 1*3 0*3 2 0*8 1 0 0 1 0*5 1 0*8 2 0*3 2*3 1*3 0 2 0 2 2 1 2*3 0 0 2 0*4 2 0*3 1 0 0 1 2 0*4 1 0 0 2 0*5 2 0*4 1 0 2 1 2 0*3 2 2 1 2*3 0*3 1 0*3 2 0*6 2 1 0*7 1 0*7 1 0*7 1 0*7 1 0*8 1 0*7 1 0*7 1 0*7 1 0*8 1 0*8 1 0*7 1 0*7 1 0*7 1 0*8 1 0*7 1 0*7 1 0 0 1 0*4 1 0*7 1 0 0 1 0*4 1 0 0 1 0*5 1 1 0*6 1 0*9 1 0*7 1"), .\and (24), .outputs(8)) IDEC: pin names not known; wires that end beside it: {INSTR[31], INSTR[20], INSTR[7:2]}, {X0, S4_1_0, S4_1_1, S10_5, X11, S19_12, S30_20, X31}
  LED J (.in(CLF_p2[0]));
  LED B (.in(BR));
  LED U (.in(CLF_p2[1]));
  LED S1 (.in(CTR));
  LED S0 (.in(d_ff_1_qn));
  Multiplexer multiplexer_3 (.in0(INSTR[30]), .in1(xor_1_out), .out(COND), .sel(BR));
  xor xor_1 (xor_1_out, INSTR[12], multiplexer_2_out);
  Register #(.trigger("high"), .width(5)) V_RS1 (.D(RS1), .clk(1'b1));  // open: en, Q, clr
  assign RS2 = {5{S2E}} & INSTR[24:20];  // AND_Gate and_6, 5 bits wide
  or or_1 (ILL, rom_1_data[21], ILL_I);
  Register #(.trigger("high"), .width(5)) V_RS2 (.D(RS2), .clk(1'b1));  // open: en, Q, clr
  assign bit_extender_1_out = {{11{CSR_EN}}, CSR_EN};  // Bit_Extender bit_extender_1
  and and_7 (and_7_out[5], S10_5, nSHIFT);
  assign bit_extender_2_out = {{18{X31}}, X31};  // Bit_Extender bit_extender_2
  Register #(.trigger("high"), .width(12)) V_CSRI (.D(CSRI), .clk(1'b1));  // open: en, Q, clr
  assign CSRI = INSTR[31:20] & bit_extender_1_out;  // AND_Gate and_8, 12 bits wide
  assign and_9_out = {4{S4_1_1}} & INSTR[11:8];  // AND_Gate and_9, 4 bits wide
  assign and_10_out = INSTR[24:21] & {4{S4_1_0}};  // AND_Gate and_10, 4 bits wide
  not not_1 (not_1_out, S19_12);
  Multiplexer #(.width(8)) multiplexer_4 (
    .in0(INSTR[19:12]), .in1(bit_extender_2_out[7:0]), .out(multiplexer_4_out), .sel(not_1_out));
  Multiplexer #(.width(11)) multiplexer_5 (
    .in0(bit_extender_2_out[18:8]), .in1(INSTR[30:20]), .out(multiplexer_5_out), .sel(S30_20));
  assign or_2_out = and_9_out | and_10_out;  // OR_Gate or_2, 4 bits wide
  assign and_11_out = INSTR[30:25] & {6{and_7_out[5]}};  // AND_Gate and_11, 6 bits wide
  Multiplexer #(.width(32)) multiplexer_6 (
    .in0({X31, multiplexer_5_out, multiplexer_4_out, X11, and_11_out, or_2_out, X0}),
    .in1(bit_extender_3_out), .out(IMM), .sel(CSRI_t));
  assign bit_extender_3_out = {{27{1'b0}}, INSTR[19:15]};  // Bit_Extender bit_extender_3
  Register #(.trigger("high"), .width(32)) V_IMM (.D(IMM), .clk(1'b1));  // open: en, Q, clr

  // Other names for the same wires on the sheet: OP[4:0] = INSTR[6:2]; P7 = INSTR[7]; P11_7[4:0] = INSTR[11:7];
  //   CSR = CSR_EN; STE = HOLD; P31 = INSTR[31]; P14_12[2:0] = INSTR[14:12]; P19_15[4:0] = INSTR[19:15];
  //   P20 = INSTR[20]; P24_20[4:0] = INSTR[24:20]; P24_21[3:0] = INSTR[24:21]; P25 = INSTR[25];
  //   P30_25[5:0] = INSTR[30:25]; P30 = INSTR[30]; P11_8[3:0] = INSTR[11:8]

  // Notes on the sheet:
  //   OP [0]
  //   OP [1]
  //   OP [6:2]
  //   rd/imm [11:7]
  //   funct3/imm [14:12]
  //   rs1/imm [19:15]
  //   rs2/imm [24:20]
  //   funct7/imm [31:25]
  //   [13]
  //   contents of rom_1 (hex, n*v repeats v):
  //   20 200020 200020 20 160 1e0 200020 200020 20 200020 200020 200020 60 160 10*200020 20 20 200020 20
  //   20 200020 200020 200020 20 200020 200020 20 14d 1e0 200020 200020 20 200020 200020 200020 4d 160
  //   10*200020 20 200020 200020 20 20 200020 200020 200020 20 200020 200020 200020 170 1e0 200020 200020
  //   20 200020 200020 200020 70 160 13*200020 20 20 7*200020 171 1e0 6*200020 71 160 13*200020 20 20
  //   200020 200020 200020 20 200020 200020 200020 16c 1e0 6*200020 6c 160 10*200020 20 200020 200020 20
  //   4*200020 20 200020 200020 200020 14e 1e0 6*200020 4e 160 10*200020 20 200020 200020 20 20 7*200020
  //   16a 1e0 6*200020 6a 160 10*200020 20 200020 200020 20 20 7*200020 16b 1e0 6*200020 6b 160 10*200020
  //   20 200020 200020 20 20 200020 200020 200020 20 200020 200020 20 160 1e0 200020 200020 20 200020
  //   200020 200020 62 160 10*200020 20 20 200020 20 20 200020 200020 200020 20 200020 200020 20 200020
  //   1e0 200020 200020 20 200020 200020 200020 63 160 10*200020 20 200020 200020 20 20 200020 200020
  //   200020 20 200020 200020 200020 170 1e0 200020 200020 20 200020 200020 200020 65 160 13*200020 20 20
  //   7*200020 171 1e0 6*200020 64 160 13*200020 20 20 200020 200020 200020 20 200020 200020 200020 16c
  //   1e0 6*200020 66 160 10*200020 20 200020 200020 20 4*200020 20 4*200020 1e0 6*200020 67 160 10*200020
  //   20 200020 200020 20 20 7*200020 16a 1e0 6*200020 68 160 10*200020 20 200020 200020 20 20 7*200020
  //   16b 1e0 6*200020 69 160 10*200020 20 200020 200020 20 20 200020 200020 200020 20 200020 200020 20
  //   160 1e0 200020 200020 20 200020 200020 200020 61 160 10*200020 20 20 200020 20 20 200020 200020
  //   200020 20 200020 200020 20 200020 1e0 200020 200020 20 4*200020 160 10*200020 20 200020 200020 20 20
  //   200020 200020 200020 20 200020 200020 200020 170 1e0 200020 200020 20 4*200020 160 13*200020 20 20
  //   7*200020 171 1e0 7*200020 160 13*200020 20 20 200020 200020 200020 20 200020 200020 200020 16c 1e0
  //   7*200020 160 10*200020 20 200020 200020 20 4*200020 20 200020 200020 200020 14f 1e0 6*200020 4f 160
  //   10*200020 20 200020 200020 20 20 7*200020 16a 1e0 7*200020 160 10*200020 20 200020 200020 20 20
  //   7*200020 16b 1e0 7*200020 160 10*200020 20 200020 200020 20 20 200020 200020 200020 20 200020 200020
  //   20 160 1e0 200020 200020 20 4*200020 160 10*200020 20 20 200020 20 20 200020 200020 200020 20 200020
  //   200020 20 200020 1e0 200020 200020 20 4*200020 160 10*200020 20 200020 200020 20 20 200020 200020
  //   200020 20 200020 200020 200020 170 1e0 200020 200020 20 4*200020 160 13*200020 20 20 7*200020 171
  //   1e0 7*200020 160 13*200020 20 20 200020 200020 200020 20 200020 200020 200020 16c 1e0 7*200020 160
  //   10*200020 20 200020 200020 20 4*200020 20 4*200020 1e0 7*200020 160 10*200020 20 200020 200020 20 20
  //   7*200020 16a 1e0 7*200020 160 10*200020 20 200020 200020 20 20 7*200020 16b 1e0 7*200020 160
  //   10*200020 20 200020 200020 20 20 1027*200020
  //   [14]
  //   [12]
endmodule

module ControlStatusRegisters (
  input  CLR,
  input  EINT,
  input  [31:0] PC,
  input  [31:0] CAUSE_IN,
  input  TRAP,
  input  CLK,
  input  OPIMM,
  input  [31:0] RX,
  input  [31:0] IMM,
  input  [11:0] CSR,
  input  BIT,
  input  CSE,
  output EIE,
  output [31:0] CSR_OUT,
  output ILL,
  output [31:0] EPC
);

  wire and_5_out, and_6_out, and_7_out, comparator_1_eq, decoder_1_out0, decoder_1_out1, decoder_1_out2,
       decoder_1_out3, decoder_1_out4, decoder_1_out5, decoder_1_out7, EPC_t, MIE, nand_1_out, not_1_out,
       or_2_out, or_3_out, RES, TMP, WR;
  wire [4:0] rom_1_data;
  wire [31:0] and_2_out, and_3_out, and_4_out, bit_extender_1_out, bit_extender_2_out, CSRV, IEB,
       multiplexer_2_out, multiplexer_3_out, not_2_out, not_3_out, not_4_out, or_1_out, R_CAUSE_q, R_TEMP_q;

  assign bit_extender_1_out = {{31{BIT}}, BIT};  // Bit_Extender bit_extender_1
  assign bit_extender_2_out = {{31{CLR}}, CLR};  // Bit_Extender bit_extender_2
  not not_1 (not_1_out, EINT);
  Register #(.trigger("high"), .width(32)) V_IN (.D(CSRV), .clk(1'b1));  // open: en, Q, clr
  assign not_2_out = ~CSRV;  // NOT_Gate not_2, 32 bits wide
  assign not_3_out = ~bit_extender_1_out;  // NOT_Gate not_3, 32 bits wide
  assign not_4_out = ~bit_extender_2_out;  // NOT_Gate not_4, 32 bits wide
  and and_1 (IEB[11], not_1_out, EIE);
  assign and_2_out = bit_extender_1_out & CSR_OUT & not_2_out;  // AND_Gate and_2, 32 bits wide
  assign and_3_out = CSRV & not_3_out;  // AND_Gate and_3, 32 bits wide
  assign and_4_out = CSRV & not_4_out;  // AND_Gate and_4, 32 bits wide
  // Probe on or_1_out
  LED #(.active("false")) F_RX (.in(OPIMM));
  LED F_IMM (.in(OPIMM));
  Register #(.trigger("high"), .width(12)) V_CSR (.D(CSR), .clk(1'b1));  // open: en, Q, clr
  assign or_1_out = and_2_out | and_3_out | and_4_out;  // OR_Gate or_1, 32 bits wide
  Multiplexer #(.width(32)) multiplexer_1 (.in0(RX), .in1(IMM), .out(CSRV), .sel(OPIMM));
  Multiplexer #(.width(32)) multiplexer_2 (.in0(or_1_out), .in1(IEB), .out(multiplexer_2_out), .sel(TRAP));
  and and_5 (and_5_out, MIE, WR);
  Multiplexer #(.width(32)) multiplexer_3 (.in0(or_1_out), .in1(PC), .out(multiplexer_3_out), .sel(TRAP));
  and and_6 (and_6_out, EPC_t, WR);
  Comparator #(.mode("unsigned"), .width(32)) comparator_1 (
    .a(CSRV), .b({32{1'b0}}), .eq(comparator_1_eq));  // open: gt, lt
  nand nand_1 (nand_1_out, comparator_1_eq, BIT);
  // Probe on multiplexer_2_out
  Register #(.width(32)) R_IE (
    .D(multiplexer_2_out), .en(or_2_out), .clk(CLK), .Q({IEB[31:12], EIE, IEB[10:0]}));  // open: clr
  or or_2 (or_2_out, TRAP, and_5_out);
  Register #(.width(32)) R_TEMP (.D(or_1_out), .en(and_7_out), .clk(CLK), .Q(R_TEMP_q));  // open: clr
  and and_7 (and_7_out, WR, TMP);
  Register #(.width(32)) R_EPC (.D(multiplexer_3_out), .en(or_3_out), .clk(CLK), .Q(EPC));  // open: clr
  or or_3 (or_3_out, TRAP, and_6_out);
  Register #(.width(32)) R_CAUSE (.D(CAUSE_IN), .en(TRAP), .clk(CLK), .Q(R_CAUSE_q));  // open: clr
  ROM #(.addrWidth(13), .dataWidth(5)) rom_1 (.addr({WR, CSR}), .data(rom_1_data));
  and and_8 (WR, nand_1_out, CSE);
  LED F_WR (.in(WR));
  assign CSR_OUT = MIE ? {IEB[31:12], EIE, IEB[10:0]} : 32'bz;  // Controlled_Buffer controlled_buffer_1
  assign CSR_OUT = TMP ? R_TEMP_q : 32'bz;  // Controlled_Buffer controlled_buffer_2
  assign CSR_OUT = EPC_t ? EPC : 32'bz;  // Controlled_Buffer controlled_buffer_3
  assign CSR_OUT = RES ? R_CAUSE_q : 32'bz;  // Controlled_Buffer controlled_buffer_4
  assign CSR_OUT = decoder_1_out0 ? {32{1'b0}} : 32'bz;  // Controlled_Buffer controlled_buffer_5
  assign CSR_OUT = decoder_1_out1 ? 32'h63687a79 : 32'bz;  // Controlled_Buffer controlled_buffer_6
  assign CSR_OUT = decoder_1_out2 ? 32'h1000 : 32'bz;  // Controlled_Buffer controlled_buffer_7
  assign CSR_OUT = decoder_1_out3 ? 32'h1 : 32'bz;  // Controlled_Buffer controlled_buffer_8
  Decoder #(.enable("false"), .select(4)) decoder_1 (
    .out0(decoder_1_out0), .out1(decoder_1_out1), .out2(decoder_1_out2), .out3(decoder_1_out3),
    .out4(decoder_1_out4), .out5(decoder_1_out5), .out6(MIE), .out7(decoder_1_out7), .out8(TMP),
    .out9(EPC_t), .out10(RES), .sel(rom_1_data[3:0]));  // open: out11, out12, out13, out14, out15
  assign CSR_OUT = decoder_1_out4 ? {32{1'b0}} : 32'bz;  // Controlled_Buffer controlled_buffer_9
  assign CSR_OUT = decoder_1_out5 ? 32'h40001100 : 32'bz;  // Controlled_Buffer controlled_buffer_10
  assign CSR_OUT = decoder_1_out7 ? 32'hfffffff0 : 32'bz;  // Controlled_Buffer controlled_buffer_11
  and and_9 (ILL, rom_1_data[4], CSE);
  LED F_MIE (.in(MIE));
  LED F_TMP (.in(TMP));
  LED F_EPC (.in(EPC_t));
  LED F_RES (.in(RES));

  // Other names for the same wires on the sheet: IEV[31:0] = {IEB[31:12], EIE, IEB[10:0]}; INT = TRAP;
  //   PCV[31:0] = EPC

  // Notes on the sheet:
  //   contents of rom_1 (hex, n*v repeats v):
  //   769*10 5 10 10 6 7 58*10 8 9 a 3022*10 1 2 3 4 1004*10 5 10 10 6 7 58*10 8 9 a 3261*10
endmodule

module InterruptController (
  input  JMP,
  input  INT,
  input  EIE,
  input  CLK,
  input  SUP,
  input  [31:0] EPC,
  input  [31:0] JAL,
  input  RST,
  output SET,
  output IRQ,
  output STALL,
  output FLUSH,
  output [31:0] CAUSE,
  output [31:0] ADDR,
  output EINT
);

  wire CLK_t, CLR, decoder_2_out0, decoder_2_out1, decoder_2_out2, EINT_t, IRQ_t, nor_1_out, nor_2_out,
       not_1_out, or_1_out, or_2_out, priority_encoder_1_en_out, RST_t;
  wire [1:0] counter_1_q;
  wire [2:0] ISR;

  LED F_EIE (.in(EIE));
  nor nor_1 (nor_1_out, nor_2_out, INT);
  not not_1 (not_1_out, EIE);
  assign ADDR = priority_encoder_1_en_out ? JAL : 32'bz;  // Controlled_Buffer controlled_buffer_1
  Priority_Encoder priority_encoder_1 (
    .in0(EINT_t), .in7(RST), .out(ISR), .gs(IRQ_t), .en_out(priority_encoder_1_en_out));  // open: in1, in2, in3, in4, in5, in6, en_in
  LED F_EINT (.in(nor_2_out));
  D_Flip_Flop d_ff_1 (.D(nor_2_out), .clk(CLK_t), .Q(EINT_t));  // open: Qn, preset, reset
  nor nor_2 (nor_2_out, nor_1_out, not_1_out);
  not not_2 (CLK_t, CLK);
  Decoder #(.select(3)) decoder_1 (
    .out0(EINT), .out7(RST_t), .sel(ISR), .en(IRQ_t));  // open: out1, out2, out3, out4, out5, out6
  assign CAUSE = EINT ? 32'h1000000b : 32'bz;  // Controlled_Buffer controlled_buffer_2
  assign CAUSE = RST_t ? {32{1'b0}} : 32'bz;  // Controlled_Buffer controlled_buffer_3
  Counter #(.max('h3), .width(2)) counter_1 (
    .clr(CLR), .count(or_1_out), .clk(CLK_t), .Q(counter_1_q));  // open: load, up, D, carry
  or or_1 (or_1_out, IRQ_t, counter_1_q[0], counter_1_q[1]);
  assign ADDR = or_2_out ? 32'hfffffff0 : 32'bz;  // Controlled_Buffer controlled_buffer_4
  or or_2 (or_2_out, EINT, RST_t);
  Decoder #(.enable("false"), .select(2)) decoder_2 (
    .out0(decoder_2_out0), .out1(decoder_2_out1), .out2(decoder_2_out2), .out3(CLR), .sel(counter_1_q));
  or or_3 (SET, JMP, IRQ);
  and and_1 (IRQ, IRQ_t, decoder_2_out0);
  or or_4 (STALL, IRQ, decoder_2_out1);
  or or_5 (FLUSH, decoder_2_out2, SUP);
endmodule

module LoadStoreUnit (
  input  [31:0] INSTR,
  output ST0,
  output ST1,
  output LD1,
  output SX,
  output LD0
);

  wire nor_1_out, nor_2_out, not_1_out, not_2_out, not_3_out, not_4_out, or_1_out;

  not not_1 (not_1_out, INSTR[0]);
  not not_2 (not_2_out, INSTR[1]);
  not not_3 (not_3_out, INSTR[12]);
  not not_4 (not_4_out, INSTR[5]);
  or or_1 (or_1_out, INSTR[12], INSTR[13]);
  nor nor_1 (nor_1_out, INSTR[13], INSTR[14]);
  nor nor_2 (nor_2_out, not_1_out, not_2_out, INSTR[2], INSTR[3], INSTR[4], INSTR[6]);
  and and_1 (ST0, not_3_out, nor_2_out, INSTR[5]);
  and and_2 (ST1, INSTR[5], nor_2_out, or_1_out);
  and and_3 (LD1, not_4_out, nor_2_out, or_1_out);
  and and_4 (SX, not_4_out, nor_2_out, nor_1_out);
  and and_5 (LD0, not_4_out, nor_2_out, not_3_out);
  LED IO (.in(nor_2_out));

  // Notes on the sheet:
  //   OP [5]
  //   funct3/imm [12]
  //   funct3/imm [13]
  //   funct3/imm [14]
  //   OP [0]
  //   OP [1]
  //   OP [2]
  //   OP [3]
  //   OP [4]
  //   OP [6]
endmodule

module ResultMux (
  input  [31:0] ALU,
  input  [31:0] NPC,
  input  [31:0] MDI,
  input  [31:0] CSR,
  input  LNK,
  input  LDR,
  input  LCS,
  output [31:0] RES
);

  wire and_1_out, and_2_out, and_3_out, not_1_out, not_2_out, not_3_out;

  Register #(.trigger("high"), .width(32)) V_ALU (.D(ALU), .clk(1'b1));  // open: en, Q, clr
  Register #(.trigger("high"), .width(32)) V_NPC (.D(NPC), .clk(1'b1));  // open: en, Q, clr
  Register #(.trigger("high"), .width(32)) V_MDI (.D(MDI), .clk(1'b1));  // open: en, Q, clr
  Register #(.trigger("high"), .width(32)) V_CSR (.D(CSR), .clk(1'b1));  // open: en, Q, clr
  assign RES = and_1_out ? ALU : 32'bz;  // Controlled_Buffer controlled_buffer_1
  LED S_ALU (.in(and_1_out));
  LED S_NPC (.in(and_2_out));
  LED S_MDI (.in(and_3_out));
  LED S_CSR (.in(LCS));
  and and_1 (and_1_out, not_1_out, not_2_out, not_3_out);
  not not_1 (not_1_out, LNK);
  not not_2 (not_2_out, LDR);
  not not_3 (not_3_out, LCS);
  assign RES = and_2_out ? NPC : 32'bz;  // Controlled_Buffer controlled_buffer_2
  assign RES = and_3_out ? MDI : 32'bz;  // Controlled_Buffer controlled_buffer_3
  and and_2 (and_2_out, LNK, not_2_out, not_3_out);
  and and_3 (and_3_out, LDR, not_3_out);
  assign RES = LCS ? CSR : 32'bz;  // Controlled_Buffer controlled_buffer_4
endmodule

module StageBuffer (
  input  ILL_IN,
  input  ILL,
  input  [31:0] PC_IN,
  input  [31:0] NPC_IN,
  input  [31:0] INSTR_IN,
  input  NOP,
  input  CLK,
  output ILL_OUT,
  output [31:0] PC_OUT,
  output [31:0] NPC_OUT,
  output [31:0] INSTR,
  output [31:0] INSTR_OUT
);

  wire and_1_out, not_1_out, or_1_out;

  not not_1 (not_1_out, NOP);
  or or_1 (or_1_out, ILL_IN, ILL);
  and and_1 (and_1_out, not_1_out, or_1_out);
  Register #(.trigger("high"), .width(32)) PC (.D(PC_IN), .clk(1'b1));  // open: en, Q, clr
  Register #(.trigger("high"), .width(32)) NPC (.D(NPC_IN), .clk(1'b1));  // open: en, Q, clr
  Register #(.trigger("high"), .width(32)) INS (.D(INSTR), .clk(1'b1));  // open: en, Q, clr
  Multiplexer #(.width(32)) multiplexer_1 (.in0(INSTR_IN), .in1(32'h13), .out(INSTR), .sel(NOP));
  D_Flip_Flop d_ff_1 (.D(and_1_out), .clk(CLK), .Q(ILL_OUT));  // open: Qn, preset, reset
  LED F_ILL (.in(and_1_out));
  Register #(.width(32)) register_1 (.D(PC_IN), .clk(CLK), .Q(PC_OUT));  // open: en, clr
  Register #(.width(32)) register_2 (.D(NPC_IN), .clk(CLK), .Q(NPC_OUT));  // open: en, clr
  Register #(.width(32)) register_3 (.D(INSTR), .clk(CLK), .Q(INSTR_OUT));  // open: en, clr
endmodule

module ResultBuffer (
  input  CSE,
  input  [31:0] V_IN,
  input  [31:0] V_CSR,
  input  LD,
  input  [31:0] D_IN,
  input  EQ_IN,
  input  LT_IN,
  input  LTU_IN,
  input  CLK,
  output [31:0] ALU,
  output [31:0] MEM,
  output EQ,
  output LT,
  output LTU
);

  wire [2:0] register_1_q;
  wire [31:0] multiplexer_1_out, register_2_q, V_DIN_q;

  LED F_CSR (.in(CSE));
  Register #(.width(32)) V_ALU (.D(multiplexer_1_out), .clk(CLK), .Q(ALU));  // open: en, clr
  Multiplexer #(.width(32)) multiplexer_1 (.in0(V_IN), .in1(V_CSR), .out(multiplexer_1_out), .sel(CSE));
  Register #(.trigger("high"), .width(32)) CSR (.D(V_CSR), .clk(1'b1));  // open: en, Q, clr
  Register #(.width(3)) register_1 (.D({LTU_IN, LT_IN, EQ_IN}), .clk(CLK), .Q(register_1_q));  // open: en, clr
  LED EQ0 (.in(register_1_q[0]));
  LED LT0 (.in(register_1_q[1]));
  LED LTU0 (.in(register_1_q[2]));
  Register #(.width(32)) register_2 (.D(ALU), .clk(CLK), .Q(register_2_q));  // open: en, clr
  Register #(.width(32)) V_DIN (.D(D_IN), .clk(CLK), .Q(V_DIN_q));  // open: en, clr
  Register #(.width(3)) register_3 (.D(register_1_q), .clk(CLK), .Q({LTU, LT, EQ}));  // open: en, clr
  LED #(.active("false")) F_ALU (.in(LD));
  LED F_MEM (.in(LD));
  LED F_EQ (.in(EQ));
  LED F_LT (.in(LT));
  LED F_LTU (.in(LTU));
  Register #(.trigger("high"), .width(32)) V_MEM (.D(MEM), .clk(1'b1));  // open: en, Q, clr
  Multiplexer #(.width(32)) multiplexer_2 (.in0(register_2_q), .in1(V_DIN_q), .out(MEM), .sel(LD));
endmodule

module RetirementUnit (
  input  [31:0] INSTR,
  input  EQ,
  input  LT,
  input  LTU,
  input  CLK,
  output LD,
  output LINK,
  output WE,
  output [4:0] RD,
  output JMP,
  output SUP
);

  wire d_ff_1_q, d_ff_2_q, JMP_t, multiplexer_1_out, multiplexer_2_out, not_1_out, or_1_out, xor_1_out;

  Register #(.trigger("high"), .width(32)) V_INS (.D(INSTR), .clk(1'b1));  // open: en, Q, clr
  // PlaRom #(.Contents("1 0 2 1 0 2 2 1 0 2 0 2 2 1*4 0 1*5 2*4 1 1 0 1*5 1 0*3 1*3 0 1 0*3 1 0*3 1 0*4 1 0*5 1"), .\and (7)) WBDEC: pin names not known; wires that end beside it: INSTR[6:2], 1'b0, {WE, JMP_t, LINK, LD}
  Multiplexer multiplexer_1 (.in0(LT), .in1(LTU), .out(multiplexer_1_out), .sel(INSTR[13]));
  Multiplexer multiplexer_2 (.in0(EQ), .in1(multiplexer_1_out), .out(multiplexer_2_out), .sel(INSTR[14]));
  assign RD = {5{WE}} & INSTR[11:7];  // AND_Gate and_1, 5 bits wide
  LED COND (.in(xor_1_out));
  xor xor_1 (xor_1_out, INSTR[12], multiplexer_2_out);
  or or_1 (or_1_out, xor_1_out, LINK);
  Register #(.trigger("high"), .width(5)) V_RD (.D(RD), .clk(1'b1));  // open: en, Q, clr
  D_Flip_Flop d_ff_1 (.D(JMP), .clk(not_1_out), .Q(d_ff_1_q));  // open: Qn, preset, reset
  and and_2 (JMP, or_1_out, JMP_t);
  not not_1 (not_1_out, CLK);
  D_Flip_Flop d_ff_2 (.D(d_ff_1_q), .clk(CLK), .Q(d_ff_2_q));  // open: Qn, preset, reset
  or or_2 (SUP, JMP, d_ff_1_q, d_ff_2_q);

  // Other names for the same wires on the sheet: LNK = LINK

  // Notes on the sheet:
  //   OP[6:2]
  //   rd[11:7]
  //   funct3/imm [12]
  //   funct3/imm [13]
  //   funct3/imm [14]
endmodule

module OperandScheduler (
  input  CLK,
  input  WE,
  input  [4:0] RD,
  input  [4:0] RS1,
  input  [4:0] RS2,
  input  [4:0] WR,
  output [1:0] S1,
  output [1:0] S2
);

  wire A1, A2, A3, A4, A5, A6, A7, A8, A9, A10, A11, A12, A13, A14, A15, A16, A17, A18, A19, A20, A21, A22,
       A23, A24, A25, A26, A27, A28, A29, A30, A31, B1, B2, B3, B4, B5, B6, B7, B8, B9, B10, B11, B12, B13,
       B14, B15, B16, B17, B18, B19, B20, B21, B22, B23, B24, B25, B26, B27, B28, B29, B30, B31;
  wire [1:0] S1_t, S2_t, S3, S4, S5, S6, S7, S8, S9, S10, S11, S12, S13, S14, S15, S16, S17, S18, S19, S20,
       S21, S22, S23, S24, S25, S26, S27, S28, S29, S30, S31;

  Decoder #(.select(5)) decoder_1 (
    .out1(A1), .out2(A2), .out3(A3), .out4(A4), .out5(A5), .out6(A6), .out7(A7), .out8(A8), .out9(A9),
    .out10(A10), .out11(A11), .out12(A12), .out13(A13), .out14(A14), .out15(A15), .out16(A16), .out17(A17),
    .out18(A18), .out19(A19), .out20(A20), .out21(A21), .out22(A22), .out23(A23), .out24(A24), .out25(A25),
    .out26(A26), .out27(A27), .out28(A28), .out29(A29), .out30(A30), .out31(A31), .sel(WR), .en(WE));  // open: out0
  OperandCounter operandcounter_1 (.SEL(S8), .S0(A8), .S1(B8), .CLK(CLK));
  OperandCounter operandcounter_2 (.SEL(S16), .S0(A16), .S1(B16), .CLK(CLK));
  OperandCounter operandcounter_3 (.SEL(S24), .S0(A24), .S1(B24), .CLK(CLK));
  OperandCounter operandcounter_4 (.SEL(S1_t), .S0(A1), .S1(B1), .CLK(CLK));
  OperandCounter operandcounter_5 (.SEL(S9), .S0(A9), .S1(B9), .CLK(CLK));
  OperandCounter operandcounter_6 (.SEL(S17), .S0(A17), .S1(B17), .CLK(CLK));
  OperandCounter operandcounter_7 (.SEL(S25), .S0(A25), .S1(B25), .CLK(CLK));
  Decoder #(.enable("false"), .select(5)) decoder_2 (
    .out1(B1), .out2(B2), .out3(B3), .out4(B4), .out5(B5), .out6(B6), .out7(B7), .out8(B8), .out9(B9),
    .out10(B10), .out11(B11), .out12(B12), .out13(B13), .out14(B14), .out15(B15), .out16(B16), .out17(B17),
    .out18(B18), .out19(B19), .out20(B20), .out21(B21), .out22(B22), .out23(B23), .out24(B24), .out25(B25),
    .out26(B26), .out27(B27), .out28(B28), .out29(B29), .out30(B30), .out31(B31), .sel(RD));  // open: out0
  OperandCounter operandcounter_8 (.SEL(S2_t), .S0(A2), .S1(B2), .CLK(CLK));
  OperandCounter operandcounter_9 (.SEL(S10), .S0(A10), .S1(B10), .CLK(CLK));
  OperandCounter operandcounter_10 (.SEL(S18), .S0(A18), .S1(B18), .CLK(CLK));
  OperandCounter operandcounter_11 (.SEL(S26), .S0(A26), .S1(B26), .CLK(CLK));
  OperandCounter operandcounter_12 (.SEL(S3), .S0(A3), .S1(B3), .CLK(CLK));
  OperandCounter operandcounter_13 (.SEL(S11), .S0(A11), .S1(B11), .CLK(CLK));
  OperandCounter operandcounter_14 (.SEL(S19), .S0(A19), .S1(B19), .CLK(CLK));
  OperandCounter operandcounter_15 (.SEL(S27), .S0(A27), .S1(B27), .CLK(CLK));
  OperandCounter operandcounter_16 (.SEL(S4), .S0(A4), .S1(B4), .CLK(CLK));
  OperandCounter operandcounter_17 (.SEL(S12), .S0(A12), .S1(B12), .CLK(CLK));
  OperandCounter operandcounter_18 (.SEL(S20), .S0(A20), .S1(B20), .CLK(CLK));
  OperandCounter operandcounter_19 (.SEL(S28), .S0(A28), .S1(B28), .CLK(CLK));
  OperandCounter operandcounter_20 (.SEL(S5), .S0(A5), .S1(B5), .CLK(CLK));
  OperandCounter operandcounter_21 (.SEL(S13), .S0(A13), .S1(B13), .CLK(CLK));
  OperandCounter operandcounter_22 (.SEL(S21), .S0(A21), .S1(B21), .CLK(CLK));
  OperandCounter operandcounter_23 (.SEL(S29), .S0(A29), .S1(B29), .CLK(CLK));
  OperandCounter operandcounter_24 (.SEL(S6), .S0(A6), .S1(B6), .CLK(CLK));
  OperandCounter operandcounter_25 (.SEL(S14), .S0(A14), .S1(B14), .CLK(CLK));
  OperandCounter operandcounter_26 (.SEL(S22), .S0(A22), .S1(B22), .CLK(CLK));
  OperandCounter operandcounter_27 (.SEL(S30), .S0(A30), .S1(B30), .CLK(CLK));
  Multiplexer #(.select(5), .width(2)) multiplexer_1 (
    .in0(2'b00), .in1(S1_t), .in2(S2_t), .in3(S3), .in4(S4), .in5(S5), .in6(S6), .in7(S7), .in8(S8),
    .in9(S9), .in10(S10), .in11(S11), .in12(S12), .in13(S13), .in14(S14), .in15(S15), .in16(S16), .in17(S17),
    .in18(S18), .in19(S19), .in20(S20), .in21(S21), .in22(S22), .in23(S23), .in24(S24), .in25(S25),
    .in26(S26), .in27(S27), .in28(S28), .in29(S29), .in30(S30), .in31(S31), .out(S1), .sel(RS1));
  OperandCounter operandcounter_28 (.SEL(S7), .S0(A7), .S1(B7), .CLK(CLK));
  OperandCounter operandcounter_29 (.SEL(S15), .S0(A15), .S1(B15), .CLK(CLK));
  OperandCounter operandcounter_30 (.SEL(S23), .S0(A23), .S1(B23), .CLK(CLK));
  OperandCounter operandcounter_31 (.SEL(S31), .S0(A31), .S1(B31), .CLK(CLK));
  Multiplexer #(.select(5), .width(2)) multiplexer_2 (
    .in0(2'b00), .in1(S1_t), .in2(S2_t), .in3(S3), .in4(S4), .in5(S5), .in6(S6), .in7(S7), .in8(S8),
    .in9(S9), .in10(S10), .in11(S11), .in12(S12), .in13(S13), .in14(S14), .in15(S15), .in16(S16), .in17(S17),
    .in18(S18), .in19(S19), .in20(S20), .in21(S21), .in22(S22), .in23(S23), .in24(S24), .in25(S25),
    .in26(S26), .in27(S27), .in28(S28), .in29(S29), .in30(S30), .in31(S31), .out(S2), .sel(RS2));

  // Other names for the same wires on the sheet: R1[4:0] = RS1; R2[4:0] = RS2
endmodule

module OperandMux (
  input  [1:0] SEL_X,
  input  [31:0] REG_X,
  input  [31:0] ALU_IN,
  input  [31:0] MEM_IN,
  input  [31:0] REG_Y,
  input  [1:0] SEL_Y,
  output [31:0] OUT_X,
  output [31:0] OUT_Y
);

  wire decoder_1_out0, decoder_1_out1, decoder_1_out2, decoder_2_out0, decoder_2_out1, decoder_2_out2;

  LED X_REG (.in(decoder_1_out0));
  LED X_ALU (.in(decoder_1_out1));
  LED X_MEM (.in(decoder_1_out2));
  Decoder #(.enable("false"), .select(2)) decoder_1 (
    .out0(decoder_1_out0), .out1(decoder_1_out1), .out2(decoder_1_out2), .sel(SEL_X));  // open: out3
  Multiplexer #(.select(2), .width(32)) multiplexer_1 (
    .in0(REG_X), .in1(ALU_IN), .in2(MEM_IN), .in3({32{1'b0}}), .out(OUT_X), .sel(SEL_X));
  Multiplexer #(.select(2), .width(32)) multiplexer_2 (
    .in0(REG_Y), .in1(ALU_IN), .in2(MEM_IN), .in3({32{1'b0}}), .out(OUT_Y), .sel(SEL_Y));
  LED Y_REG (.in(decoder_2_out0));
  Decoder #(.enable("false"), .select(2)) decoder_2 (
    .out0(decoder_2_out0), .out1(decoder_2_out1), .out2(decoder_2_out2), .sel(SEL_Y));  // open: out3
  LED Y_ALU (.in(decoder_2_out1));
  LED Y_MEM (.in(decoder_2_out2));
  Register #(.trigger("high"), .width(32)) RX (.D(OUT_X), .clk(1'b1));  // open: en, Q, clr
  Register #(.trigger("high"), .width(32)) RY (.D(OUT_Y), .clk(1'b1));  // open: en, Q, clr
endmodule

module OperandCounter (
  input  S0,
  input  S1,
  input  CLK,
  output [1:0] SEL
);

  wire or_1_out, or_2_out;

  Counter #(.max('h3), .width(2)) counter_1 (
    .load(or_1_out), .count(or_2_out), .clk(CLK), .D({1'b0, S1}), .Q(SEL));  // open: clr, up, carry
  or or_1 (or_1_out, S0, S1);
  or or_2 (or_2_out, SEL[0], SEL[1]);
endmodule

module BinaryToBCD (
  input  [31:0] VIN,
  output [31:0] VOUT,
  output [3:0] DIGIT
);

  wire [31:4] divider_1_rem;

  Divider #(.width(32)) divider_1 (.a(VIN), .b(32'ha), .out(VOUT), .rem({divider_1_rem, DIGIT}));  // open: upper
endmodule
